# Fritzing sketch sensonation-v2 (saved by Fritzing 0.9.2b)
breadboards: 1

parts:
  Raspberry_Pi1 = Raspberry Pi B rev2
  S1 = SWITCH-MOMENTARY-2 [package=reed_switch_pth]
  S2 = SWITCH-MOMENTARY-2 [package=reed_switch_pth]
  S13 = SWITCH-MOMENTARY-2 [package=reed_switch_pth]
  S14 = SWITCH-MOMENTARY-2 [package=reed_switch_pth]
  S15 = SWITCH-MOMENTARY-2 [package=reed_switch_pth]
  S16 = SWITCH-MOMENTARY-2 [package=reed_switch_pth]
  S17 = SWITCH-MOMENTARY-2 [package=reed_switch_pth]
  S18 = SWITCH-MOMENTARY-2 [package=reed_switch_pth]
  S19 = SWITCH-MOMENTARY-2 [package=reed_switch_pth]
  S20 = SWITCH-MOMENTARY-2 [package=reed_switch_pth]
  M2 = DC Motor
  M1 = DC Motor
  M5 = DC Motor
  M4 = DC Motor
  M3 = DC Motor
  IC1 = MCP23017 I2C I/O Expander
  IC2 = MCP23017 I2C I/O Expander
  U3 = DRV8833
  U4 = DRV8833
  U5 = DRV8833
  U6 = DRV8833
  Power_plug1 = Power plug

nets:
  VDD: Raspberry_Pi1.5V, IC1.VDD, IC1.A2, IC1.RESET, IC2.VDD, IC2.RESET
  N1: Raspberry_Pi1.GPIO_2, IC1.SDA, IC2.SDA
  N2: Raspberry_Pi1.GPIO_3, IC1.SCL, IC2.SCL
  VSS: Raspberry_Pi1.GND, S1.2, S2.2, S13.2, S14.2, S15.2, S16.2, S17.2, S18.2, S19.2, S20.2, IC1.VSS, IC1.A0, IC1.A1, IC2.VSS, IC2.A0, IC2.A1, IC2.A2, U3.GND#0, U4.GND#0, U5.GND#0, U6.GND#0
  N3: S1.1, IC2.GPA7
  N4: S2.1, IC2.GPA6
  N5: S13.1, IC2.GPA3
  N6: S14.1, IC2.GPA4
  N7: S15.1, IC2.GPA2
  N8: S16.1, IC2.GPA5
  N9: S17.1, IC1.GPA7
  N10: S18.1, IC2.GPA0
  N11: S19.1, IC1.GPA6
  N12: S20.1, IC2.GPA1
  N13: M2.pin_1, U3.AOUT2
  N14: M2.pin_2, U3.AOUT1
  N15: M1.pin_1, U3.BOUT1
  N16: M1.pin_2, U3.BOUT2
  N17: M5.pin_1, U5.BOUT1
  N18: M5.pin_2, U5.BOUT2
  N19: M4.pin_1, U4.AOUT2
  N20: M4.pin_2, U4.AOUT1
  N21: M3.pin_1, U4.BOUT1
  N22: M3.pin_2, U4.BOUT2
  N23: IC1.GPB0, U5.BIN1
  N24: IC1.GPB1, U5.BIN2
  N25: IC1.GPB2, U5.AIN2
  N26: IC1.GPB3, U5.AIN1
  N27: IC1.GPB4, U6.BIN1
  N28: IC1.GPB5, U6.BIN2
  N29: IC1.GPB6, U6.AIN2
  N30: IC1.GPB7, U6.AIN1
  N31: IC2.GPB0, U3.BIN1
  N32: IC2.GPB1, U3.BIN2
  N33: IC2.GPB2, U3.AIN2
  N34: IC2.GPB3, U3.AIN1
  N35: IC2.GPB4, U4.BIN1
  N36: IC2.GPB5, U4.BIN2
  N37: IC2.GPB6, U4.AIN2
  N38: IC2.GPB7, U4.AIN1
  N39: U3.GND#8, U4.GND#8, U5.GND#8, U6.GND#8, Power_plug1.GND
  VIN: U3.VIN, U4.VIN, U5.VIN, U6.VIN, Power_plug1.VCC

custom parts:
  MCP23017 I2C I/O Expander: The MCP23017 uses two i2c pins (these can be shared with other i2c devices), and in exchange gives you 16 general purpose pins. You can set each of 16 pins to be input, output, input with a pullup or open drain. There's even the ability to get an interrupt via an external pin when any of the inputs change so you don't have to keep polling the chip.
  DRV8833: The DRV8833 provides a dual bridge motor driver solution for toys, printers, and other mechatronic applications.
